// Logisim project teste.circ as structural Verilog: 3 circuits, main circuit main
module main (
  input  [3:0] in_1,
  input  [3:0] in_2,
  output out_3,
  output [3:0] out_4
);

  // Probe on in_1
  ADD_4 add_4_1 (.out_4(out_4), .in_2(in_1), .out_3(out_3), .in_1(in_2));
  // Probe on out_4
  // Probe on in_2
endmodule

module ADD_1 (
  input  A,
  input  B,
  input  VEM_1,
  output out_4,
  output out_5
);

  wire and_1_out, and_2_out, or_1_out, xor_1_out;

  xor xor_1 (xor_1_out, A, B);
  or or_1 (or_1_out, A, B);
  and and_1 (and_1_out, A, B);
  and and_2 (and_2_out, or_1_out, VEM_1);
  xor xor_2 (out_4, xor_1_out, VEM_1);
  or or_2 (out_5, and_2_out, and_1_out);
endmodule

module ADD_4 (
  input  [3:0] in_1,
  input  [3:0] in_2,
  output out_3,
  output [3:0] out_4
);

  wire add_1_2_out_5, add_1_3_out_5, add_1_4_out_5;

  // Probe on in_2
  ADD_1 add_1_1 (.A(in_1[3]), .B(in_2[3]), .VEM_1(add_1_2_out_5), .out_4(out_4[3]), .out_5(out_3));
  ADD_1 add_1_2 (.A(in_1[2]), .B(in_2[2]), .VEM_1(add_1_3_out_5), .out_4(out_4[2]), .out_5(add_1_2_out_5));
  ADD_1 add_1_3 (.A(in_1[1]), .B(in_2[1]), .VEM_1(add_1_4_out_5), .out_4(out_4[1]), .out_5(add_1_3_out_5));
  // Probe on out_4
  ADD_1 add_1_4 (.A(in_1[0]), .B(in_2[0]), .VEM_1(1'b0), .out_4(out_4[0]), .out_5(add_1_4_out_5));
  // Probe on in_1
endmodule
